# Fritzing sketch diagram (saved by Fritzing 1.0.0rc)
breadboards: 1

parts:
  M1 = RioRand LM2596
  JACK1 = 2.1mm Barrel Jack with Terminal Block
  Pololu_A1 = Pololu A4988 [package=SO16]
  C3 = Electrolytic Capacitor [capacitance=100µF voltage=16V package="100 mil [THT, electrolytic]"]
  U1 = ESP8266 ESP-01 Upgraded WiFi Module [part_number=ESP8266]
  M2 = Stepper Motor - Bipolar

nets:
  N1: M1.Pin_1, JACK1.POS, Pololu_A1.VMOT, C3.+
  N2: M1.Pin_2, JACK1.NEG, Pololu_A1.GND#14, C3.-
  VDD: M1.Pin_3, Pololu_A1.MS1, Pololu_A1.MS2, Pololu_A1.MS3, Pololu_A1.DIR, Pololu_A1.VDD, U1.VCC, U1.CH_PD
  N3: M1.Pin_4, Pololu_A1.GND#8, U1.GND
  N4: Pololu_A1.ENABLE, U1.GPIO_2
  N5: Pololu_A1.RESET, Pololu_A1.SLEEP
  N6: Pololu_A1.STEP, U1.GPIO_0
  N7: Pololu_A1.1B, M2.D
  N8: Pololu_A1.1A, M2.B
  N9: Pololu_A1.2A, M2.C
  N10: Pololu_A1.2B, M2.A

notes:
  12 V DC input
  3.3 V DC output
  100µF
  A4988
  DC-DC buck converter
  Stepper motor
  ESP8266-01

custom parts:
  ESP8266 ESP-01 Upgraded WiFi Module: Upgraded Version ESP-01,all Flash are upgraded to 1M byte.Also support Cloud service remote transmission.
